# Fritzing sketch Telegram_MonitoringPJU (saved by Fritzing 0.9.3b)

parts:
  U1 = NodeMCU V3.0
  Part1 = ADS1115
  U2 = Module 4 Relais 5V [package="Module 4 Relais 5V"]
  Part2 = ACS712 Current Sensor 5A 20A 30A
  Part3 = ACS712 Current Sensor 5A 20A 30A
  A1 = photosensitive ldr module [package=THT]
  A2 = photosensitive ldr module [package=THT]
  LED1 = LEDs [package=led10mm]
  LED2 = LEDs [package=led10mm]
  J1 = 220v plug

nets:
  N1: U1.D1, Part1.SCL
  N2: U1.D2, Part1.SDA
  VCC: U1.3V3, Part1.VDD, Part2.VCC, Part3.VCC, A1.pin4, A2.pin4
  GND: U1.GND, Part1.GND, U2.GND, Part2.GND, Part3.GND, A1.pin3, A2.pin3
  N3: U1.D6, U2.IN1
  N4: U1.D7, U2.IN4
  N5: U1.VU, U2.VCC
  N6: Part1.A0, U2.K1-NO, Part3.2, Part3.OUT
  N7: Part1.A1, U2.K4-NO, Part2.2, Part2.OUT
  N8: Part1.A2, A2.pin2
  N9: Part1.A3, A1.pin2
  N10: U2.K1-NF, U2.K4-NF, J1.pin1
  N11: Part2.1, LED2.C
  N12: Part3.1, LED1.C
  N13: LED1.A, LED2.A, J1.pin2

custom parts:
  NodeMCU V3.0: ESP8266 based NodeMCU
  ADS1115: ADC ADS1115
  Module 4 Relais 5V: Module 4 Relais 5V 4x SPD-06VDC-SD-C
  ACS712 Current Sensor 5A 20A 30A: Remix by Michael Kubina http://www.kubina.info Original by: https://forum.fritzing.org/t/current-sensor-5a-acs712/7694 https://forum.fritzing.org/u/ArtHome ArtHome12@gmail.com
  photosensitive ldr module: The LDR Sensor Module is used to detect the presence of light / measuring the intensity of light. The output of the module goes high in the presence of light and it becomes low in the absence of light. The sensitivity of signal detection can be adjusted using a potentiometer.
  LEDs: LEDs Standard schematic elements and footprints for 5mm, 3mm, 1206, and 0603 sized LEDs. 5mm - Spark Fun Electronics SKU : COM-00529 (and others)
  220v plug: Generic 220V AC plug.
